// Logisim project homework1.circ as structural Verilog: 2 circuits, main circuit main
module driver (
  input  [3:0] Qin,
  input  Pin,
  output a,
  output b,
  output p,
  output c,
  output d,
  output e,
  output f,
  output g
);

  wire and_1_out, and_2_out, and_3_out, and_4_out, and_5_out, and_6_out, and_7_out, and_8_out, and_9_out,
       and_10_out, and_11_out, and_12_out, and_13_out, and_14_out, and_15_out, and_16_out, not_1_out;

  and and_1 (and_1_out, ~Qin[0], ~Qin[2]);  // AND_Gate
  and and_2 (and_2_out, Qin[0], Qin[2]);
  and and_3 (and_3_out, Qin[1], Qin[0]);
  and and_4 (and_4_out, ~Qin[1], ~Qin[0]);  // AND_Gate
  and and_5 (and_5_out, ~Qin[2], ~Qin[0]);  // AND_Gate
  and and_6 (and_6_out, Qin[1], ~Qin[0]);  // AND_Gate
  and and_7 (and_7_out, ~Qin[2], Qin[1]);  // AND_Gate
  and and_8 (and_8_out, ~Qin[1], Qin[2], Qin[0]);  // AND_Gate
  and and_9 (and_9_out, ~Qin[2], ~Qin[0]);  // AND_Gate
  and and_10 (and_10_out, Qin[1], ~Qin[0]);  // AND_Gate
  and and_11 (and_11_out, ~Qin[1], ~Qin[0]);  // AND_Gate
  and and_12 (and_12_out, Qin[2], ~Qin[1]);  // AND_Gate
  and and_13 (and_13_out, Qin[2], ~Qin[0]);  // AND_Gate
  and and_14 (and_14_out, Qin[2], ~Qin[1]);  // AND_Gate
  and and_15 (and_15_out, ~Qin[2], Qin[1]);  // AND_Gate
  and and_16 (and_16_out, Qin[1], ~Qin[0]);  // AND_Gate
  or or_1 (a, and_1_out, and_2_out, Qin[1], Qin[3]);
  not not_1 (not_1_out, Qin[2]);
  or or_2 (b, not_1_out, and_3_out, and_4_out);
  or or_3 (c, Qin[2], Qin[0], ~Qin[1]);  // OR_Gate
  or or_4 (d, Qin[3], and_5_out, and_6_out, and_7_out, and_8_out);
  or or_5 (e, and_9_out, and_10_out);
  or or_6 (f, Qin[3], and_11_out, and_12_out, and_13_out);
  or or_7 (g, Qin[3], and_14_out, and_15_out, and_16_out);
  _7_Segment_Display u_7_segment_display_1 (.g(g), .f(f), .a(a), .b(b), .e(e), .d(d), .c(c), .dp(Pin));

  assign p = Pin;
endmodule

module main (
);

  wire button_1_out, counter_1_carry, driver_1_a, driver_1_b, driver_1_c, driver_1_d, driver_1_e, driver_1_f,
       driver_1_g, driver_1_p;
  wire [3:0] counter_1_q;

  Counter #(.width(4), .max('h9)) counter_1 (
    .count(button_1_out), .Q(counter_1_q), .carry(counter_1_carry), .clk(button_1_out));  // open: load, D, clr
  Button button_1 (.out(button_1_out));
  driver driver_1 (
    .Qin(counter_1_q), .Pin(counter_1_carry), .a(driver_1_a), .b(driver_1_b), .c(driver_1_c), .d(driver_1_d),
    .e(driver_1_e), .f(driver_1_f), .g(driver_1_g), .p(driver_1_p));
  _7_Segment_Display u_7_segment_display_1 (
    .g(driver_1_g), .f(driver_1_f), .a(driver_1_a), .b(driver_1_b), .e(driver_1_e), .d(driver_1_d),
    .c(driver_1_c), .dp(driver_1_p));
endmodule
